// Logisim project decode.circ as structural Verilog
module decode (
  input  [23:0] instru,
  input  We
);

  registry_24bits registry_24bits_1 (.instru(instru), .We(We));  // open: S
endmodule
